// Digital circuit CPU.dig as structural Verilog
module CPU (
  input  clk,
  input  clk_2,
  input  [31:0] Interface
);

  wire button_1_out, Clk_t, counter_1_ovf, Ctrl_Alloc, Ctrl_AllocOut, Ctrl_BusMux0, Ctrl_BusMux1,
       Ctrl_Dealloc, Ctrl_InterfaceOut, Ctrl_LoadInst, Ctrl_MemAddrIn, Ctrl_MemDataIn, Ctrl_MemDataOut,
       Ctrl_SetFirstBlock, dipswitch_1_out, Hold, or_2_out, or_3_out, or_4_out, ShadCp_Active,
       ShadCp_Activen, ShadCpClk;
  wire [1:0] dipswitch_27_out, mmu_1_memstr, multiplexer_2_out;
  wire [3:0] counter_2_out;
  wire [7:0] Instruction_q;
  wire [23:0] Address, MemoryAddr_q, multiplexer_3_out, ShadCp_Addr;
  wire [28:8] multiplexer_6_out;
  wire [31:0] Boot_Sequencer_d, Bus, Bus_Unmuxed, Bytecode_Executor_d, MemAddrIn_out, mmu_1_memaddr,
       mmu_1_memdataout;

  PullDown #(.Bits(32)) pulldown_1 (.out(Bus_Unmuxed));
  Multiplexer #(.Selector_Bits(2), .Bits(32)) multiplexer_1 (
    .sel({Ctrl_BusMux1, Ctrl_BusMux0}), .in_0(Bus_Unmuxed), .in_1({Bus_Unmuxed[23:0], Bus_Unmuxed[31:24]}),
    .in_2({Bus_Unmuxed[15:0], Bus_Unmuxed[31:16]}),
    .in_3({Bus_Unmuxed[7:0], Bus_Unmuxed[31:16], Bus_Unmuxed[7:0]}), .out(Bus));
  PullDown #(.Bits(32)) pulldown_2 (.out(Bus));
  and and_1 (ShadCpClk, clk, ShadCp_Active);
  not not_1 (ShadCp_Active, ShadCp_Activen);
  MMU mmu_1 (
    .Ctrl_Alloc(Ctrl_Alloc), .Ctrl_Dealloc(Ctrl_Dealloc), .Ctrl_AllocOut(Ctrl_AllocOut),
    .Ctrl_SetFirst(Ctrl_SetFirstBlock), .Clk(Clk_t), .Bus(Bus), .MemDataIn(mmu_1_memdataout),
    .MemAddr(mmu_1_memaddr), .MemDataOut(mmu_1_memdataout), .MemStr(mmu_1_memstr[0]),
    .MemLd(mmu_1_memstr[1]), .CPU_Enable(Hold));
  Counter #(.Bits(24)) counter_1 (
    .en(ShadCp_Active), .C(ShadCpClk), .clr(1'b0), .out(ShadCp_Addr), .ovf(counter_1_ovf));
  or or_1 (ShadCp_Activen, ShadCp_Activen, counter_1_ovf);
  Register #(.Bits(24)) MemoryAddr (.D(Bus[23:0]), .C(Clk_t), .en(Ctrl_MemAddrIn), .Q(MemoryAddr_q));
  Multiplexer #(.Bits(2)) multiplexer_2 (
    .sel(Hold), .in_0(mmu_1_memstr), .in_1({Ctrl_MemDataOut, Ctrl_MemDataIn}), .out(multiplexer_2_out));
  Multiplexer #(.Bits(24)) multiplexer_3 (
    .sel(Hold), .in_0(MemoryAddr_q), .in_1(mmu_1_memaddr[23:0]), .out(multiplexer_3_out));
  Multiplexer #(.Bits(24)) multiplexer_4 (
    .sel(ShadCp_Activen), .in_0(ShadCp_Addr), .in_1(multiplexer_3_out), .out(Address));
  or or_2 (or_2_out, ShadCp_Active, multiplexer_2_out[0]);
  or or_3 (or_3_out, ShadCpClk, Clk_t);
  ROM #(.bigEndian("true"), .AddrBits(24), .Bits(32)) Boot_ROM (.A(Address), .sel(ShadCp_Active), .D(mmu_1_memdataout));
  RAMSinglePort #(.AddrBits(24), .Bits(32)) ramsingleport_1 (
    .A(Address), .str(or_2_out), .C(or_3_out), .ld(multiplexer_2_out[1]), .D(mmu_1_memdataout));
  Button button_1 (.out(button_1_out));
  DipSwitch dipswitch_1 (.out(dipswitch_1_out));
  assign Bus_Unmuxed = or_4_out ? mmu_1_memdataout : 32'bz;  // Driver driver_1
  assign mmu_1_memdataout = Ctrl_MemDataIn ? Bus : 32'bz;  // Driver driver_2
  Multiplexer multiplexer_5 (.sel(dipswitch_1_out), .in_0(button_1_out), .in_1(clk_2), .out(Clk_t));
  or or_4 (or_4_out, Ctrl_MemDataOut, ShadCp_Active);
  Seven_Seg_Hex seven_seg_hex_1 (.d(Address[23:20]), .dp(1'b0));
  Seven_Seg_Hex seven_seg_hex_2 (.d(Address[19:16]), .dp(1'b0));
  Seven_Seg_Hex seven_seg_hex_3 (.d(Address[15:12]), .dp(1'b0));
  Seven_Seg_Hex seven_seg_hex_4 (.d(Address[11:8]), .dp(1'b0));
  Seven_Seg_Hex seven_seg_hex_5 (.d(Address[7:4]), .dp(1'b0));
  Seven_Seg_Hex seven_seg_hex_6 (.d(Address[3:0]), .dp(1'b0));
  Counter #(.Bits(4)) counter_2 (.en(Hold), .C(Clk_t), .clr(1'b0), .out(counter_2_out));  // open: ovf
  Register #(.Bits(8)) Instruction (.D(Bus[7:0]), .C(Clk_t), .en(Ctrl_LoadInst), .Q(Instruction_q));
  Seven_Seg_Hex seven_seg_hex_7 (.d(Bus[31:28]), .dp(1'b0));
  Seven_Seg_Hex seven_seg_hex_8 (.d(Bus[27:24]), .dp(1'b0));
  Seven_Seg_Hex seven_seg_hex_9 (.d(Bus[23:20]), .dp(1'b0));
  ROM #(.AddrBits(4), .Bits(32)) Boot_Sequencer (.A(counter_2_out), .sel(1'b1), .D(Boot_Sequencer_d));
  ROM #(.AddrBits(12), .Bits(32)) Bytecode_Executor (
    .A({Instruction_q, counter_2_out}), .sel(1'b1), .D(Bytecode_Executor_d));
  Seven_Seg_Hex seven_seg_hex_10 (.d(Bus[19:16]), .dp(1'b0));
  DipSwitch MemAddrIn (.out(MemAddrIn_out[0]));
  DipSwitch MemDataIn (.out(MemAddrIn_out[1]));
  DipSwitch MemDataOut (.out(MemAddrIn_out[2]));
  DipSwitch Alloc (.out(MemAddrIn_out[3]));
  DipSwitch Dealloc (.out(MemAddrIn_out[4]));
  DipSwitch SetFirstBlock (.out(MemAddrIn_out[5]));
  DipSwitch AllocOut (.out(MemAddrIn_out[6]));
  DipSwitch LoadInstr (.out(MemAddrIn_out[7]));
  DipSwitch dipswitch_2 (.out(MemAddrIn_out[8]));
  DipSwitch dipswitch_3 (.out(MemAddrIn_out[9]));
  DipSwitch dipswitch_4 (.out(MemAddrIn_out[10]));
  DipSwitch dipswitch_5 (.out(MemAddrIn_out[11]));
  DipSwitch dipswitch_6 (.out(MemAddrIn_out[12]));
  DipSwitch dipswitch_7 (.out(MemAddrIn_out[13]));
  DipSwitch dipswitch_8 (.out(MemAddrIn_out[14]));
  DipSwitch dipswitch_9 (.out(MemAddrIn_out[15]));
  DipSwitch dipswitch_10 (.out(MemAddrIn_out[16]));
  DipSwitch dipswitch_11 (.out(MemAddrIn_out[17]));
  DipSwitch dipswitch_12 (.out(MemAddrIn_out[18]));
  DipSwitch dipswitch_13 (.out(MemAddrIn_out[19]));
  DipSwitch dipswitch_14 (.out(MemAddrIn_out[20]));
  DipSwitch dipswitch_15 (.out(MemAddrIn_out[21]));
  DipSwitch dipswitch_16 (.out(MemAddrIn_out[22]));
  DipSwitch dipswitch_17 (.out(MemAddrIn_out[23]));
  DipSwitch dipswitch_18 (.out(MemAddrIn_out[24]));
  DipSwitch dipswitch_19 (.out(MemAddrIn_out[25]));
  DipSwitch dipswitch_20 (.out(MemAddrIn_out[26]));
  DipSwitch dipswitch_21 (.out(MemAddrIn_out[27]));
  DipSwitch dipswitch_22 (.out(MemAddrIn_out[28]));
  DipSwitch dipswitch_23 (.out(MemAddrIn_out[29]));
  DipSwitch dipswitch_24 (.out(MemAddrIn_out[30]));
  DipSwitch dipswitch_25 (.out(MemAddrIn_out[31]));
  Seven_Seg_Hex seven_seg_hex_11 (.d(Bus[15:12]), .dp(1'b0));
  Seven_Seg_Hex seven_seg_hex_12 (.d(Bus[11:8]), .dp(1'b0));
  DipSwitch dipswitch_26 (.out(dipswitch_27_out[0]));
  DipSwitch dipswitch_27 (.out(dipswitch_27_out[1]));
  Multiplexer #(.Selector_Bits(2), .Bits(32)) multiplexer_6 (
    .sel(dipswitch_27_out), .in_0(Boot_Sequencer_d), .in_1(Bytecode_Executor_d), .in_2(MemAddrIn_out),
    .in_3(MemAddrIn_out),
    .out({Ctrl_InterfaceOut, Ctrl_BusMux1, Ctrl_BusMux0, multiplexer_6_out, Ctrl_LoadInst, Ctrl_AllocOut, Ctrl_SetFirstBlock, Ctrl_Dealloc, Ctrl_Alloc, Ctrl_MemDataOut, Ctrl_MemDataIn, Ctrl_MemAddrIn}));
  assign Bus_Unmuxed = Ctrl_InterfaceOut ? Interface : 32'bz;  // Driver driver_3
  Seven_Seg_Hex seven_seg_hex_13 (.d(Bus[7:4]), .dp(1'b0));
  Seven_Seg_Hex seven_seg_hex_14 (.d(Bus[3:0]), .dp(1'b0));

  // Notes on the sheet:
  //   clk: Hz: 2147483647
  //   clk_2: Hz: 10
  //   Bus Muxer
  //   ABCD
  //   BCDA
  //   CDAB
  //   DABC
  //   Memory
  //   Boot_ROM loads boot.spy
  //   Memory Address
  //   Control
  //   Bus
  //   Boot_Sequencer loads ucodeBootSeq.bin
endmodule
