// Digital circuit MMU.dig as structural Verilog
module MMU (
  input  Ctrl_Alloc,
  input  Ctrl_Dealloc,
  input  Ctrl_AllocOut,
  input  [31:0] Bus,
  input  [31:0] MemDataIn,
  input  Clk,
  output [31:0] MemAddr,
  output [31:0] MemDataOut,
  output MemStr,
  output MemLd
);

  wire comparator_1_eq, comparator_1_gt, or_1_out, Step_ovf;
  wire [5:0] Step_out;
  wire [23:0] Microcode_d;
  wire [31:0] Available_q, Desired_q, First_q, Next_q, Previous_q, sub_1_s, Testing_q;

  Register #(.Bits(3)) State (.D(Microcode_d[23:21]), .C(Clk), .en(Microcode_d[20]), .Q(Step_out[5:3]));
  Counter #(.Bits(3)) Step (.en(1'b1), .C(Clk), .clr(Step_ovf), .out(Step_out[2:0]), .ovf(Step_ovf));
  ROM #(.bigEndian("true"), .AddrBits(6), .Bits(24)) Microcode (
    .A(Step_out), .sel(1'b1), .D({Microcode_d[23:15], MemStr, MemLd, Microcode_d[12:0]}));
  // Probe on {Microcode_d[23:15], MemStr, MemLd, Microcode_d[12:0]}
  Register #(.Bits(32)) Available (.D(MemDataIn), .C(Clk), .en(Microcode_d[0]), .Q(Available_q));
  assign MemDataIn = Microcode_d[1] ? Available_q : 32'bz;  // Driver driver_1
  Register #(.Bits(32)) Desired (.D(Bus), .C(Clk), .en(Microcode_d[2]), .Q(Desired_q));
  assign MemDataIn = Microcode_d[3] ? Desired_q : 32'bz;  // Driver driver_2
  Register #(.Bits(32)) register_1 (.D(MemDataIn), .C(Clk), .en(Microcode_d[12]), .Q(MemAddr));
  Comparator #(.Bits(32)) comparator_1 (
    .a(Available_q), .b(Desired_q), .gt(comparator_1_gt), .eq(comparator_1_eq));  // open: lt
  Sub #(.Bits(32)) sub_1 (.a(Available_q), .b(Desired_q), .c_i(1'b0), .s(sub_1_s));  // open: c_o
  assign MemDataOut = MemStr ? MemDataIn : 32'bz;  // Driver driver_3
  or or_1 (or_1_out, comparator_1_gt, comparator_1_eq);
  Register #(.Bits(32)) First (.D(MemDataIn), .C(Clk), .en(Microcode_d[4]), .Q(First_q));
  Register #(.Bits(32)) Previous (.D(MemDataIn), .C(Clk), .en(Microcode_d[6]), .Q(Previous_q));
  Register #(.Bits(32)) Testing (.D(MemDataIn), .C(Clk), .en(Microcode_d[8]), .Q(Testing_q));
  Register #(.Bits(32)) Next (.D(MemDataIn), .C(Clk), .en(Microcode_d[10]), .Q(Next_q));
  assign MemDataIn = Microcode_d[5] ? First_q : 32'bz;  // Driver driver_4
  assign MemDataIn = Microcode_d[7] ? Previous_q : 32'bz;  // Driver driver_5
  assign MemDataIn = Microcode_d[9] ? Testing_q : 32'bz;  // Driver driver_6
  assign MemDataIn = Microcode_d[11] ? Next_q : 32'bz;  // Driver driver_7

  // Notes on the sheet:
  //   Microcode loads MMU-ucode.bin
  //   Sufficient
  //   Difference
endmodule
